// Logisim project smips.circ as structural Verilog
module Board (
);

  wire CLK, HALT, MEM_WE, RESET, TTY_WE;
  wire [3:0] MEM_BE;
  wire [6:0] TTY_DATA;
  wire [31:0] MEM_ADDR, MEM_RDATA, MEM_WDATA;

  Clock Reloj (.out(CLK));
  Button u_Reset (.out(RESET));
  CPU cpu_1 (
    .CLK(CLK), .RESET(RESET), .MEM_RDATA(MEM_RDATA), .MEM_ADDR(MEM_ADDR), .MEM_WDATA(MEM_WDATA),
    .MEM_BE(MEM_BE), .MEM_WE(MEM_WE), .TTY_DATA(TTY_DATA), .TTY_WE(TTY_WE), .HALT(HALT));
  TTY #(.cols(48), .rows(12)) tty_1 (.data(TTY_DATA), .clk(CLK), .we(TTY_WE), .clr(RESET));
  Memory memory_1 (.CLK(CLK), .ADDR(MEM_ADDR), .WDATA(MEM_WDATA), .BE(MEM_BE), .WE(MEM_WE), .RDATA(MEM_RDATA));
  LED u_Halt (.in(HALT));

  // Notes on the sheet:
  //   S-MIPS | Board
  //   No modificar: la CPU se implementa dentro del subcircuito CPU.
endmodule

module CPU (
  input  CLK,
  input  RESET,
  input  [31:0] MEM_RDATA,
  output [31:0] MEM_ADDR,
  output [31:0] MEM_WDATA,
  output [3:0] MEM_BE,
  output MEM_WE,
  output [6:0] TTY_DATA,
  output TTY_WE,
  output HALT
);

  wire [4:0] Rd, Rs, Rt, Shamt;
  wire [5:0] Funct, Op;
  wire [15:0] Imm16;

  Instruction_Decoder instruction_decoder_1 (
    .Imm16(Imm16), .Op(Op), .Rs(Rs), .Rt(Rt), .Rd(Rd), .Shamt(Shamt), .Funct(Funct));  // open: IR_IN

  // Notes on the sheet:
  //   CPU S-MIPS: implementar aqui
  //   No cambiar nombres, anchos ni sentido de los pines: la placa depende de ellos.
endmodule

module Memory (
  input  CLK,
  input  [31:0] ADDR,
  input  [31:0] WDATA,
  input  [3:0] BE,
  input  WE,
  output [31:0] RDATA
);

  RAM #(.addrWidth(12), .asyncread("true"), .byteenables("byteEnables"), .dataWidth(32), .\type ("nonvolatile")) Main_Memory (
    .addr(ADDR[13:2]), .we(WE), .oe(1'b1), .clk(CLK), .din(WDATA), .dout(RDATA), .be3(BE[3]), .be2(BE[2]),
    .be1(BE[1]), .be0(BE[0]));

  // Other names for the same wires on the sheet: A[11:0] = ADDR[13:2]

  // Notes on the sheet:
  //   Memoria unificada: 4096 palabras de 32 bits (16 KiB), little-endian
  //   Lectura combinacional; escritura en el flanco de subida de CLK con WE=1, solo en los bytes con BE=1.
  //   Se usan los bits 13..2 de ADDR; los demas se ignoran (el espacio se repite cada 16 KiB).
endmodule

module Datapath (
  input  [4:0] Shamt,
  input  RegWrite,
  input  [31:0] MEM_DATA,
  output [31:0] MEM_WDATA,
  output [31:0] MEM_ADDR,
  output [3:0] MEM_BE,
  output [31:0] PC_OUT
);

  wire CLK, IRWrite, PCWrite, RESET;
  wire [15:0] Imm16;
  wire [31:0] A_q, alu_1_result, B_q, bit_extender_1_out, bit_extender_2_out, MDROUT, multiplexer_2_out,
       PCOUT, register_file_1_read_data1, register_file_1_read_data2;

  Register #(.width(32)) IR (.en(IRWrite), .clk(CLK), .clr(RESET));  // open: D, Q
  Register_File register_file_1 (
    .READ_DATA1(register_file_1_read_data1), .READ_DATA2(register_file_1_read_data2));  // open: CLK, RESET, REG_WRITE, READ_ADDR1, READ_ADDR2, WRITE_ADDR, WRITE_DATA
  Register #(.width(32)) MDR (.D(MEM_DATA), .clk(CLK), .Q(MDROUT));  // open: en, clr
  Register #(.width(32)) A (.D(register_file_1_read_data1), .Q(A_q));  // open: en, clk, clr
  Register #(.width(32)) B (.D(register_file_1_read_data2), .clk(CLK), .Q(B_q));  // open: en, clr
  Register #(.width(32)) PC (.en(PCWrite), .clk(CLK), .Q(PCOUT), .clr(RESET));  // open: D
  assign bit_extender_1_out = {{16{Imm16[15]}}, Imm16};  // Bit_Extender bit_extender_1
  assign bit_extender_2_out = {{27{Shamt[4]}}, Shamt};  // Bit_Extender bit_extender_2
  Multiplexer #(.select(2), .width(32)) multiplexer_1 (
    .in0(B_q), .in1(32'h4), .in2(bit_extender_1_out));  // open: in3, out, sel
  Multiplexer #(.select(2), .width(32)) multiplexer_2 (
    .in0(PCOUT), .in1(A_q), .in2(bit_extender_2_out), .out(multiplexer_2_out));  // open: in3, sel
  ALU alu_1 (.A(multiplexer_2_out), .RESULT(alu_1_result));  // open: B, ALU_OP, ZERO
  Register #(.width(32)) ALUOUT (.D(alu_1_result), .clk(CLK));  // open: en, Q, clr

  // Notes on the sheet:
  //   ALUSrcB
  //   ALUSrcA
endmodule

module Instruction_Decoder (
  input  [31:0] IR_IN,
  output [15:0] Imm16,
  output [5:0] Op,
  output [4:0] Rs,
  output [4:0] Rt,
  output [4:0] Rd,
  output [4:0] Shamt,
  output [5:0] Funct
);


  assign Funct = IR_IN[5:0];
  assign Imm16 = IR_IN[15:0];
  assign Op = IR_IN[31:26];
  assign Rd = IR_IN[15:11];
  assign Rs = IR_IN[25:21];
  assign Rt = IR_IN[20:16];
  assign Shamt = IR_IN[10:6];
endmodule

// VHDL entity Register_File, as the project stores it:
library ieee;
use ieee.std_logic_1164.all;
use ieee.numeric_std.all;

entity Register_File is
    port (
        -- Control y sincronizacion
        CLK        : in  std_logic;
        RESET      : in  std_logic;
        REG_WRITE  : in  std_logic;

        -- Puerto de Lectura 1
        READ_ADDR1 : in  std_logic_vector(4 downto 0);
        READ_DATA1 : out std_logic_vector(31 downto 0);

        -- Puerto de Lectura 2
        READ_ADDR2 : in  std_logic_vector(4 downto 0);
        READ_DATA2 : out std_logic_vector(31 downto 0);

        -- Puerto de Escritura
        WRITE_ADDR : in  std_logic_vector(4 downto 0);
        WRITE_DATA : in  std_logic_vector(31 downto 0)
    );
end entity Register_File;

architecture RTL of Register_File is

    -- Array de 31 registros de 32 bits (el registro 0 se maneja de forma especial)
    type register_array is array (1 to 31) of std_logic_vector(31 downto 0);
    signal registers : register_array := (others => (others => '0'));

begin

    -- Proceso secuencial: Escritura sincrona y reset (R6)
    process (CLK)
    begin
        if rising_edge(CLK) then
            if RESET = '1' then
                registers     <= (others => (others => '0'));
                registers(28) <= x"00001800"; -- $gp inicial
                registers(29) <= x"00003FFC"; -- $sp inicial
            elsif REG_WRITE = '1' then
                if unsigned(WRITE_ADDR) /= 0 then
                    registers(to_integer(unsigned(WRITE_ADDR))) <= WRITE_DATA;
                end if;
            end if;
        end if;
    end process;

    -- Puerto de Lectura 1: Combinacional con proteccion estricta para $zero
    process (READ_ADDR1, registers)
    begin
        if unsigned(READ_ADDR1) = 0 then
            READ_DATA1 <= (others => '0');
        else
            READ_DATA1 <= registers(to_integer(unsigned(READ_ADDR1)));
        end if;
    end process;

    -- Puerto de Lectura 2: Combinacional con proteccion estricta para $zero
    process (READ_ADDR2, registers)
    begin
        if unsigned(READ_ADDR2) = 0 then
            READ_DATA2 <= (others => '0');
        else
            READ_DATA2 <= registers(to_integer(unsigned(READ_ADDR2)));
        end if;
    end process;

end architecture RTL;

// VHDL entity ALU, as the project stores it:
library ieee;
use ieee.std_logic_1164.all;
use ieee.numeric_std.all;

entity ALU is
    port (
        A      : in  std_logic_vector(31 downto 0);
        B      : in  std_logic_vector(31 downto 0);
        ALU_OP : in  std_logic_vector(2 downto 0);
        RESULT : out std_logic_vector(31 downto 0);
        ZERO   : out std_logic
    );
end entity ALU;

architecture RTL of ALU is
begin
    process(A, B, ALU_OP)
        variable signed_a     : signed(31 downto 0);
        variable signed_b     : signed(31 downto 0);
        variable unsigned_b   : unsigned(31 downto 0);
        variable res_internal : std_logic_vector(31 downto 0);
        variable shift_amt    : integer range 0 to 31;
    begin
        -- Conversiones explícitas para operaciones con y sin signo
        signed_a     := signed(A);
        signed_b     := signed(B);
        unsigned_b   := unsigned(B);
        
        -- Extracción del factor de desplazamiento (shamt) desde los bits bajos de B
        shift_amt    := to_integer(unsigned(B(4 downto 0)));
        
        res_internal := (others => '0');

        case ALU_OP is
            when "000" => -- Suma (add, addi, addu, addiu, lw, sw, cálculo de direcciones)
                res_internal := std_logic_vector(signed_a + signed_b);
                
            when "001" => -- Resta (sub, beq, bne)
                res_internal := std_logic_vector(signed_a - signed_b);
                
            when "010" => -- Comparación con signo (slt, slti)
                if signed_a < signed_b then
                    res_internal := x"00000001";
                else
                    res_internal := x"00000000";
                end if;
                
            when "011" => -- Operación AND lógico (and, andi)
                res_internal := A and B;
                
            when "100" => -- Operación OR lógico (or, ori)
                res_internal := A or B;
                
            when "101" => -- Desplazamiento lógico a la izquierda (sll)
                res_internal := std_logic_vector(shift_left(unsigned_b, shift_amt));
                
            when "110" => -- Desplazamiento lógico a la derecha (srl, entran ceros)
                res_internal := std_logic_vector(shift_right(unsigned_b, shift_amt));
                
            when others =>
                res_internal := (others => '0');
        end case;

        -- Asignación de la salida de resultado
        RESULT <= res_internal;

        -- Generación de la bandera ZERO requerida por la arquitectura[span_4](start_span)[span_4](end_span)
        if res_internal = x"00000000" then
            ZERO <= '1';
        else
            ZERO <= '0';
        end if;
    end process;

end architecture RTL;
